# Fritzing sketch Hardware (saved by Fritzing 0.9.3b)
breadboards: 1

parts:
  Part1 = Arduino Uno (Rev3)
  LED1 = LED - 5mm [color="Red (633nm)" package="5 mm [THT]"]
  LED2 = LED - 5mm [color="Red (633nm)" package="5 mm [THT]"]
  LED3 = LED - 5mm [color="Red (633nm)" package="5 mm [THT]"]
  J1 = Piezo Speaker
  U1 = POT_SWITCH [package=pot_pth_switch]
  LCD1 = LCD screen
  R1 = Resistor [tolerance=±5% resistance=220 package=THT]
  R2 = Resistor [tolerance=±5% resistance=220 package=THT]
  R3 = Resistor [tolerance=±5% resistance=220 package=THT]
  R4 = Resistor [tolerance=±5% resistance=220 package=THT]

nets (from the breadboard view):
  N1: Part1.A0, LED2.anode, LCD1.V0, R2.Pin_0
  N2: Part1.D9_PWM, LED3.cathode
  N3: Part1.D10_PWM/SS, LED2.cathode
  N4: Part1.D11_PWM/MOSI, LED1.cathode
  GND: Part1.D13/SCK, Part1.GND, U1.G$2_2, LCD1.VSS, LCD1.R/W, LCD1.LED-, R1.Pin_1, R2.Pin_1, R3.Pin_1
  N5: Part1.D2, LCD1.RS
  N6: Part1.D3_PWM, LCD1.E
  N7: Part1.D4, LCD1.DB7
  N8: Part1.D5_PWM, LCD1.DB6
  N9: Part1.D6_PWM, LCD1.DB5
  N10: Part1.D7, LCD1.DB4
  5V: Part1.5V, U1.G$1_A, LCD1.VDD, R4.Pin_0
  N11: LED1.anode, R1.Pin_0
  N12: LED3.anode, R3.Pin_0
  N13: J1.pin1, J1.pin2
  N14: LCD1.LED+, R4.Pin_1
